# Fritzing sketch servo potentiometer (saved by Fritzing 0.9.3b)
breadboards: 1

parts:
  Part1 = Adafruit Feather M0 Express [part_number="Adafruit #3403"]
  R1 = Rotary Potentiometer (Small) [maximum_resistance=100kΩ package=THT]
  R2 = Resistor [tolerance=±5% resistance=2.2k package=THT]
  J1 = Basic Servo

nets:
  GND: Part1.GND, R1.leg2, J1.gnd
  N1: Part1.A3, J1.pulse
  N2: Part1.A1, R2.Pin_0
  +3V3: Part1.+3V3, R1.leg1, J1.vcc
  N3: R1.wiper, R2.Pin_1

custom parts:
  Adafruit Feather M0 Express: We love all our Feathers equally, but this Feather is very special. It's our first Feather that is specifically designed for use with CircuitPython! CircuitPython is our beginner-oriented flavor of MicroPython - and as the name hints at, its a small but full-featured version of the popular Python programming language specifically for use with circuitry and electronics. That doesn't mean you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
